# Fritzing sketch automatic-test-bench (saved by Fritzing 1.0.3b)
breadboards: 1

parts:
  Part1 = Arduino Uno (Rev3)
  Raspberry_Pi_1 = Raspberry Pi 3 [part_number=RPI-3-V1.2]  # not connected
  CONN1 = USB connector [package=THT]
  CONN2 = USB connector [package=THT]
  S1 = Pushbutton [package="[THT]"]
  S2 = Pushbutton [package="[THT]"]
  YF-S201_Flow_Meter1 = YF-S201 Water Flow Meter
  WeMos_D1_Mini_Relay_Shield_V1 = WeMos D1 Mini Relay Shield V2  # not connected
  M1 = RioRand LM2596
  Power_plug1 = Power plug
  M2 = DC Motor [voltage_(max)=6V voltage_(min)=3V]
  HC-SR04_Sensor_1 = HC-SR04 Ultrasonic Distance Sensor

nets:
  N1: Part1.D8, HC-SR04_Sensor_1.TRIG
  N2: Part1.D9_PWM, HC-SR04_Sensor_1.ECHO
  N3: Part1.D2, YF-S201_Flow_Meter1.SIG
  N4: Part1.D3_PWM, S1.Pin_1, S1.Pin_2
  N5: Part1.D4, S2.Pin_1, S2.Pin_2
  VCC: Part1.5V, YF-S201_Flow_Meter1.VCC, HC-SR04_Sensor_1.VCC
  5V: CONN1.5V, CONN2.5V
  N6: CONN1.d-, CONN2.d-
  N7: CONN1.d+, CONN2.d+
  N8: CONN1.GND, CONN1.chassis5, CONN2.chassis5, CONN2.chassis6
  GND: S1.Pin_3, S1.Pin_4, S2.Pin_3, S2.Pin_4, YF-S201_Flow_Meter1.GND, HC-SR04_Sensor_1.GND
  N9: M1.Pin_1, Power_plug1.VCC
  N10: M1.Pin_2, Power_plug1.GND, M2.pin_2

notes:
  regulated to 5v
  12v 5A power source
  JD-VCC
  GND
  Relay power is isolated from arduino by using JD_VCC pin
  IN1
  VCC
  water pump

custom parts:
  YF-S201 Water Flow Meter: The YF-S201 Flow Meter. The input voltage is 5V to 24V (DC).
