# Fritzing sketch mock-test-bench (saved by Fritzing 1.0.3b)

parts:
  Part1 = Arduino Uno (Rev3)  # not connected
  Raspberry_Pi_1 = Raspberry Pi 3 [part_number=RPI-3-V1.2]  # not connected
  CONN1 = USB connector [package=THT]
  CONN2 = USB connector [package=THT]

nets:
  5V: CONN1.5V, CONN2.5V
  N1: CONN1.d-, CONN2.d-
  N2: CONN1.d+, CONN2.d+
  N3: CONN1.GND, CONN1.chassis5, CONN2.chassis5, CONN2.chassis6
